# Fritzing sketch motor_control (saved by Fritzing 0.8.7b)
breadboards: 1

parts:
  Part1 = Arduino Uno (Rev3)
  Q1 = NPN-Transistor [package="TO92 [THT]"]
  R1 = Resistor [tolerance=±5% resistance=220 package=THT]
  M1 = DC Motor

nets:
  N1: Part1.D3_PWM, R1.Pin_0
  N2: Part1.GND, Q1.E
  N3: Part1.VIN, M1.pin_2
  N4: Q1.B, R1.Pin_1
  N5: Q1.C, M1.pin_1
