# Fritzing sketch plant_watering (saved by Fritzing 0.9.4)
breadboards: 1

parts:
  Part1 = Arduino Uno (Rev3)
  Q1 = NPN-Transistor [package="TO92 [THT]"]
  R1 = Resistor [tolerance=±5% resistance=220 package=THT]
  M1 = DC Motor
  Part2 = Soil Moisture Sensor

nets:
  N1: Part1.A0, Part2.SIG
  N2: Part1.D3_PWM, R1.Pin_0
  5V: Part1.5V, Q1.E, Part2.VCC
  GND: Part1.GND, Part2.GND
  N3: Q1.B, R1.Pin_1
  N4: Q1.C, M1.pin_1
