# Fritzing sketch weather_dht22 (saved by Fritzing 0.9.4)
breadboards: 1

parts:
  Part1 = Arduino Uno (Rev3)
  R1 = Resistor [tolerance=±5% resistance=10k package=THT]
  DHT1 = DHT22 Humidity and Temperature Sensor

nets:
  N1: Part1.D2, R1.Pin_1, DHT1.DATA
  5V: Part1.5V, R1.Pin_0, DHT1.VDD
  GND: Part1.GND, DHT1.GND

// code stored in the sketch: weather_dht22.ino
#include "utility.hpp"

#define PIN_DHT 2
#define TYPE_DHT DHT22

DHT dht(PIN_DHT, TYPE_DHT);

float temperature = 0;
float humidity = 0;
float feelsLike = 0;

// the setup function runs once on power or reset
void setup() {
  // begin the DHT temperature sensor
  dht.begin();
  // begin serial connection for data transmission
  Serial.begin(9600);
  // wait for serial monitor
  while (!Serial);
}

// the loop function loops forever
void loop() {
  // read temperature
  temperature = dht.readTemperature();
  // read humidity
  humidity = dht.readHumidity();
  // calculate heat index
  feelsLike = dht.computeHeatIndex(temperature, humidity);
  // if the values are not read correctly
  if (isnan(temperature) || isnan(humidity) || isnan(feelsLike)) {
    Serial.println(F("Failed to read from DHT sensor!"));
    return;
  }
  printWeatherInfo(temperature, humidity, feelsLike);
  // delay 2 seconds (DHT22 sensing period)
  delayMilliseconds(2000);
}
